# Fritzing sketch Schematic (saved by Fritzing 0.9.3b)
breadboards: 1

parts:
  Part1 = Arduino Uno (Rev3)
  Part2 = Ambient Light Sensor (TEMT6000 Breakout Board)
  S1 = Momentary Switch [package=ksa_sealed_tac_switch]
  Part3 = OLED Monochrome 128x64 1.3 inch [part_number=938]
  C1 = Capacitor [package=cap-pth-small2]
  R1 = Resistor [tolerance=±5% resistance=10k package="1206 [SMD]"]

nets:
  N1: Part1.A0, Part2.S
  N2: Part1.A4/SDA, Part3.MOSI_SDA
  N3: Part1.A5/SCL, Part3.SCLK_SCK
  3V3: Part1.AREF, Part1.3V3, Part2.VCC, Part3.VIN, R1.Pin_0
  N4: Part1.D2, S1.1, C1.2, R1.Pin_1
  N5: Part1.D4, Part3.RESET
  GND: Part1.GND, Part2.GND, S1.4, Part3.GND, C1.1

custom parts:
  OLED Monochrome 128x64 1.3 inch: These displays are small, only about 1.3" diagonal, but very readable due to the high contrast of an OLED display. This display is made of 128x64 individual white OLED pixels, each one is turned on or off by the controller chip. Because the display makes its own light, no backlight is required. This reduces the power required to run the OLED and is why the display has such high contrast; we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
